// Logisim project 16-bit_computer.circ as structural Verilog: 24 circuits, main circuit main
module main (
  input  [7:0] INPR
);

  wire alu_1_e_out, and_1_out, and_2_out, and_3_out, and_4_out, Clock, E, FGI, FGO, I, IEN, nor_1_out,
       not_1_out, p, R, r_t, S;
  wire [2:0] bus_control_1_bus_output;
  wire [3:0] outr_1_out_5, outr_1_out_6;
  wire [7:0] D;
  wire [11:0] B;
  wire [15:0] AC, alu_1_alu_output, ar_1_bus_out, controlled_buffer_1_out, DR, ir_1_bus_out,
       multiplexer_1_out, pc_1_bus_out, ram_1_data, T, tr_1_bus_out;

  Clock clock_1 (.out(Clock));
  ALU alu_1 (
    .E(E), .AC(AC), .INPR(INPR), .DR(DR), .r(r_t), .p(p), .ALU_Output(alu_1_alu_output), .E_out(alu_1_e_out),
    .B(B), .T(T), .D(D));
  and and_1 (and_1_out, R, T[1]);
  and and_2 (and_2_out, D[3], T[4]);
  and and_3 (and_3_out, D[5], T[4]);
  and and_4 (and_4_out, D[6], T[6]);
  AR ar_1 (.Bus_IN(multiplexer_1_out), .I(I), .D(D), .R(R), .T(T), .Clock(Clock), .Bus_OUT(ar_1_bus_out));
  and and_5 (r_t, T[3], D[7], ~I);  // AND_Gate
  and and_6 (p, T[3], D[7], I);
  OUTR outr_1 (.p(p), .B(B), .Bus_IN(multiplexer_1_out), .out_5(outr_1_out_5), .out_6(outr_1_out_6), .Clock(Clock));
  nor nor_1 (nor_1_out, and_1_out, and_2_out, and_3_out, and_4_out);
  PC pc_1 (
    .Bus_IN(multiplexer_1_out), .E(E), .FGI(FGI), .FGO(FGO), .Bus_OUT(pc_1_bus_out), .DR(DR), .AC(AC), .D(D),
    .B(B), .r(r_t), .p(p), .R_2(R), .T(T), .Clock(Clock));
  DR dr_1 (.Bus_IN(multiplexer_1_out), .Bus_OUT(DR), .T(T), .D(D), .Clock(Clock));
  E e_1 (.r(r_t), .Clock(Clock), .Cout(alu_1_e_out), .D(D), .T(T), .E(E));  // open: B, INP
  TR tr_1 (.Bus_IN(multiplexer_1_out), .R(R), .Bus_OUT(tr_1_bus_out), .T(T), .Clock(Clock));
  IR ir_1 (.Bus_IN(multiplexer_1_out), .R(R), .T(T), .B(B), .D(D), .I(I), .Bus_OUT(ir_1_bus_out), .S(S), .Clock(Clock));
  Hex_Digit_Display hex_digit_display_1 (.value(outr_1_out_5));  // open: dp
  Hex_Digit_Display hex_digit_display_2 (.value(outr_1_out_6));  // open: dp
  SC sc_1 (.p(p), .r(r_t), .R_2(R), .D(D), .INC(1'b1), .S(S), .Clock(Clock), .Clear(1'b0), .T(T));
  FGI fgi_1 (.Clock(Clock), .B(B), .p(p), .FGI(FGI));
  FGO fgo_1 (.Clock(Clock), .B(B), .p(p), .FGO(FGO));
  RAM #(.addrWidth(12), .dataWidth(16)) ram_1 (
    .addr(ar_1_bus_out[11:0]), .data(ram_1_data), .clk(Clock), .ld(nor_1_out));  // open: sel, clr
  AC ac_1 (.ALU_IN(alu_1_alu_output), .r(r_t), .p(p), .Bus_OUT(AC), .B(B), .T(T), .D(D), .Clock(Clock));
  not not_1 (not_1_out, nor_1_out);
  IEN ien_1 (.B(B), .p(p), .Clock(Clock), .R(R), .T(T), .IEN(IEN));
  R r_1 (.FGI(FGI), .FGO(FGO), .IEN(IEN), .Clock(Clock), .T(T), .R(R));
  assign controlled_buffer_1_out = nor_1_out ? ram_1_data : 16'bz;  // Controlled_Buffer controlled_buffer_1
  assign ram_1_data = not_1_out ? multiplexer_1_out : 16'bz;  // Controlled_Buffer controlled_buffer_2
  Multiplexer #(.select(3), .width(16), .enable("false")) multiplexer_1 (
    .in1(ar_1_bus_out), .in2(pc_1_bus_out), .in3(DR), .in4(AC), .in5(ir_1_bus_out), .in6(tr_1_bus_out),
    .in7(controlled_buffer_1_out), .out(multiplexer_1_out), .sel(bus_control_1_bus_output));  // open: in0
  BUS_control bus_control_1 (.B(B), .D(D), .I(I), .T(T), .R(R), .p(p), .BUS_Output(bus_control_1_bus_output));
endmodule

module Full_Adder (
  input  Ci,
  input  Ai,
  input  Bi,
  output Si,
  output Ci_1
);

  wire half_adder_1_c, half_adder_2_c, half_adder_2_s;

  Half_Adder half_adder_1 (.A(Ci), .B(half_adder_2_s), .S(Si), .C(half_adder_1_c));
  Half_Adder half_adder_2 (.A(Ai), .B(Bi), .S(half_adder_2_s), .C(half_adder_2_c));
  or or_1 (Ci_1, half_adder_1_c, half_adder_2_c);
endmodule

module _16_Adder (
  input  [15:0] A,
  input  [15:0] B,
  input  Cin,
  output [15:0] S,
  output Cout
);

  wire full_adder_1_ci_1, full_adder_3_ci_1, full_adder_4_ci_1, full_adder_5_ci_1, full_adder_6_ci_1,
       full_adder_7_ci_1, full_adder_8_ci_1, full_adder_9_ci_1, full_adder_10_ci_1, full_adder_11_ci_1,
       full_adder_12_ci_1, full_adder_13_ci_1, full_adder_14_ci_1, full_adder_15_ci_1, full_adder_16_ci_1;

  Full_Adder full_adder_1 (.Ci(full_adder_3_ci_1), .Ai(A[7]), .Bi(B[7]), .Si(S[7]), .Ci_1(full_adder_1_ci_1));
  Full_Adder full_adder_2 (.Ci(full_adder_4_ci_1), .Ai(A[15]), .Bi(B[15]), .Si(S[15]), .Ci_1(Cout));
  Full_Adder full_adder_3 (.Ci(full_adder_5_ci_1), .Ai(A[6]), .Bi(B[6]), .Si(S[6]), .Ci_1(full_adder_3_ci_1));
  Full_Adder full_adder_4 (.Ci(full_adder_6_ci_1), .Ai(A[14]), .Bi(B[14]), .Si(S[14]), .Ci_1(full_adder_4_ci_1));
  Full_Adder full_adder_5 (.Ci(full_adder_7_ci_1), .Ai(A[5]), .Bi(B[5]), .Si(S[5]), .Ci_1(full_adder_5_ci_1));
  Full_Adder full_adder_6 (.Ci(full_adder_8_ci_1), .Ai(A[13]), .Bi(B[13]), .Si(S[13]), .Ci_1(full_adder_6_ci_1));
  Full_Adder full_adder_7 (.Ci(full_adder_9_ci_1), .Ai(A[4]), .Bi(B[4]), .Si(S[4]), .Ci_1(full_adder_7_ci_1));
  Full_Adder full_adder_8 (.Ci(full_adder_10_ci_1), .Ai(A[12]), .Bi(B[12]), .Si(S[12]), .Ci_1(full_adder_8_ci_1));
  Full_Adder full_adder_9 (.Ci(full_adder_11_ci_1), .Ai(A[3]), .Bi(B[3]), .Si(S[3]), .Ci_1(full_adder_9_ci_1));
  Full_Adder full_adder_10 (.Ci(full_adder_12_ci_1), .Ai(A[11]), .Bi(B[11]), .Si(S[11]), .Ci_1(full_adder_10_ci_1));
  Full_Adder full_adder_11 (.Ci(full_adder_13_ci_1), .Ai(A[2]), .Bi(B[2]), .Si(S[2]), .Ci_1(full_adder_11_ci_1));
  Full_Adder full_adder_12 (.Ci(full_adder_14_ci_1), .Ai(A[10]), .Bi(B[10]), .Si(S[10]), .Ci_1(full_adder_12_ci_1));
  Full_Adder full_adder_13 (.Ci(full_adder_15_ci_1), .Ai(A[1]), .Bi(B[1]), .Si(S[1]), .Ci_1(full_adder_13_ci_1));
  Full_Adder full_adder_14 (.Ci(full_adder_16_ci_1), .Ai(A[9]), .Bi(B[9]), .Si(S[9]), .Ci_1(full_adder_14_ci_1));
  Full_Adder full_adder_15 (.Ci(Cin), .Ai(A[0]), .Bi(B[0]), .Si(S[0]), .Ci_1(full_adder_15_ci_1));
  Full_Adder full_adder_16 (.Ci(full_adder_1_ci_1), .Ai(A[8]), .Bi(B[8]), .Si(S[8]), .Ci_1(full_adder_16_ci_1));
endmodule

module Half_Adder (
  input  A,
  input  B,
  output S,
  output C
);

  xor xor_1 (S, A, B);
  and and_1 (C, A, B);
endmodule

module _12_Register_with_adder (
  input  [11:0] Input,
  input  Load,
  input  Clock,
  input  Clear,
  input  INC,
  output [11:0] Output
);

  wire or_1_out;
  wire [11:0] multiplexer_1_out;
  wire [15:0] inc_s;

  _16_Adder u_inc (.A({4'b0000, Output}), .B(16'h1), .Cin(1'b0), .S(inc_s));  // open: Cout
  or or_1 (or_1_out, Load, INC);
  Multiplexer #(.width(12), .enable("false")) multiplexer_1 (
    .in0(inc_s[11:0]), .in1(Input), .out(multiplexer_1_out), .sel(Load));
  Register #(.width(12)) REG (.D(multiplexer_1_out), .en(or_1_out), .Q(Output), .clk(Clock), .clr(Clear));
endmodule

module _16_Register_with_adder (
  input  [15:0] Input,
  input  Load,
  input  Clock,
  input  Clear,
  input  INC,
  output [15:0] Output
);

  wire or_1_out;
  wire [15:0] inc_s, multiplexer_1_out;

  _16_Adder u_inc (.A(Output), .B(16'h1), .Cin(1'b0), .S(inc_s));  // open: Cout
  or or_1 (or_1_out, Load, INC);
  Multiplexer #(.width(16), .enable("false")) multiplexer_1 (
    .in0(inc_s), .in1(Input), .out(multiplexer_1_out), .sel(Load));
  Register #(.width(16)) REG (.D(multiplexer_1_out), .en(or_1_out), .Q(Output), .clk(Clock), .clr(Clear));
endmodule

module Logic_control (
  input  r,
  input  p,
  input  [11:0] B,
  input  [15:0] T,
  input  [7:0] D,
  output [6:0] Instruction
);

  and AND (Instruction[0], D[0], T[5]);
  and ADD (Instruction[1], D[1], T[5]);
  and DR (Instruction[2], D[2], T[5]);
  and INPR (Instruction[3], p, B[11]);
  and COMP (Instruction[4], r, B[9]);
  and SHR (Instruction[5], r, B[7]);
  and SHL (Instruction[6], r, B[6]);
endmodule

module _1_ALU (
  input  Cin,
  input  DRi,
  input  ACi,
  input  INPRi,
  input  Ai_1,
  input  Ai_1_2,
  input  [6:0] Instruction,
  output Cout,
  output Fi
);

  wire ADD_out, AND_out, COMP_out, DR_out, Full_Adder_si, INPR_out, not_1_out, SHL_out, SHR_out;

  Full_Adder Full_Adder (.Ci(Cin), .Ai(ACi), .Bi(DRi), .Si(Full_Adder_si), .Ci_1(Cout));
  not not_1 (not_1_out, ACi);
  and AND (AND_out, DRi, Instruction[0], ACi);
  and ADD (ADD_out, Instruction[1], Full_Adder_si);
  and DR (DR_out, Instruction[2], DRi);
  and INPR (INPR_out, INPRi, Instruction[3]);
  and COMP (COMP_out, Instruction[4], not_1_out);
  and SHR (SHR_out, Instruction[5], Ai_1);
  and SHL (SHL_out, Instruction[6], Ai_1_2);
  or or_1 (Fi, AND_out, ADD_out, DR_out, INPR_out, COMP_out, SHR_out, SHL_out);

  // Other names for the same wires on the sheet: AC_i_1 = Ai_1; AC_i_1_t = Ai_1_2; AND = Instruction[0];
  //   ADD = Instruction[1]; DR = Instruction[2]; INPR = Instruction[3]; COMP = Instruction[4]; SHR = Instruction[5];
  //   SHL = Instruction[6]
endmodule

module ALU (
  input  E,
  input  [15:0] AC,
  input  [7:0] INPR,
  input  [15:0] DR,
  input  r,
  input  p,
  input  [11:0] B,
  input  [15:0] T,
  input  [7:0] D,
  output [15:0] ALU_Output,
  output E_out
);

  wire ADD_out, ALU_0_cout, ALU_1_cout, ALU_2_cout, ALU_3_cout, ALU_4_cout, ALU_5_cout, ALU_6_cout,
       ALU_7_cout, ALU_8_cout, ALU_9_cout, ALU_10_cout, ALU_11_cout, ALU_12_cout, ALU_13_cout, ALU_14_cout,
       ALU_15_cout, SHL_out, SHR_out;
  wire [6:0] Instruction;

  Logic_control Control_Unit (.r(r), .p(p), .Instruction(Instruction), .B(B), .T(T), .D(D));
  _1_ALU ALU_0 (
    .Ai_1(AC[1]), .Ai_1_2(E), .ACi(AC[0]), .INPRi(INPR[0]), .DRi(DR[0]), .Instruction(Instruction),
    .Cin(1'b0), .Cout(ALU_0_cout), .Fi(ALU_Output[0]));
  _1_ALU ALU_4 (
    .Ai_1(AC[5]), .Ai_1_2(AC[3]), .ACi(AC[4]), .INPRi(INPR[4]), .DRi(DR[4]), .Instruction(Instruction),
    .Cin(ALU_3_cout), .Cout(ALU_4_cout), .Fi(ALU_Output[4]));
  _1_ALU ALU_1 (
    .Ai_1(AC[2]), .Ai_1_2(AC[0]), .ACi(AC[1]), .INPRi(INPR[1]), .DRi(DR[1]), .Instruction(Instruction),
    .Cin(ALU_0_cout), .Cout(ALU_1_cout), .Fi(ALU_Output[1]));
  _1_ALU ALU_5 (
    .Ai_1(AC[6]), .Ai_1_2(AC[4]), .ACi(AC[5]), .INPRi(INPR[5]), .DRi(DR[5]), .Instruction(Instruction),
    .Cin(ALU_4_cout), .Cout(ALU_5_cout), .Fi(ALU_Output[5]));
  _1_ALU ALU_2 (
    .Ai_1(AC[3]), .Ai_1_2(AC[1]), .ACi(AC[2]), .INPRi(INPR[2]), .DRi(DR[2]), .Instruction(Instruction),
    .Cin(ALU_1_cout), .Cout(ALU_2_cout), .Fi(ALU_Output[2]));
  _1_ALU ALU_6 (
    .Ai_1(AC[7]), .Ai_1_2(AC[5]), .ACi(AC[6]), .INPRi(INPR[6]), .DRi(DR[6]), .Instruction(Instruction),
    .Cin(ALU_5_cout), .Cout(ALU_6_cout), .Fi(ALU_Output[6]));
  and ADD (ADD_out, ALU_15_cout, Instruction[1]);
  and SHR (SHR_out, AC[0], Instruction[5]);
  and SHL (SHL_out, Instruction[6], AC[15]);
  _1_ALU ALU_3 (
    .Ai_1(AC[4]), .Ai_1_2(AC[2]), .ACi(AC[3]), .INPRi(INPR[3]), .DRi(DR[3]), .Instruction(Instruction),
    .Cin(ALU_2_cout), .Cout(ALU_3_cout), .Fi(ALU_Output[3]));
  _1_ALU ALU_7 (
    .Ai_1(AC[8]), .Ai_1_2(AC[6]), .ACi(AC[7]), .INPRi(INPR[7]), .DRi(DR[7]), .Instruction(Instruction),
    .Cin(ALU_6_cout), .Cout(ALU_7_cout), .Fi(ALU_Output[7]));
  or or_1 (E_out, ADD_out, SHR_out, SHL_out);
  _1_ALU ALU_8 (
    .Ai_1(AC[9]), .Ai_1_2(AC[7]), .ACi(AC[8]), .INPRi(1'b0), .DRi(DR[8]), .Instruction(Instruction),
    .Cin(ALU_7_cout), .Cout(ALU_8_cout), .Fi(ALU_Output[8]));
  _1_ALU ALU_12 (
    .Ai_1(AC[13]), .Ai_1_2(AC[11]), .ACi(AC[12]), .INPRi(1'b0), .DRi(DR[12]), .Instruction(Instruction),
    .Cin(ALU_11_cout), .Cout(ALU_12_cout), .Fi(ALU_Output[12]));
  _1_ALU ALU_9 (
    .Ai_1(AC[10]), .Ai_1_2(AC[8]), .ACi(AC[9]), .INPRi(1'b0), .DRi(DR[9]), .Instruction(Instruction),
    .Cin(ALU_8_cout), .Cout(ALU_9_cout), .Fi(ALU_Output[9]));
  _1_ALU ALU_13 (
    .Ai_1(AC[14]), .Ai_1_2(AC[12]), .ACi(AC[13]), .INPRi(1'b0), .DRi(DR[13]), .Instruction(Instruction),
    .Cin(ALU_12_cout), .Cout(ALU_13_cout), .Fi(ALU_Output[13]));
  _1_ALU ALU_10 (
    .Ai_1(AC[11]), .Ai_1_2(AC[9]), .ACi(AC[10]), .INPRi(1'b0), .DRi(DR[10]), .Instruction(Instruction),
    .Cin(ALU_9_cout), .Cout(ALU_10_cout), .Fi(ALU_Output[10]));
  _1_ALU ALU_14 (
    .Ai_1(AC[15]), .Ai_1_2(AC[13]), .ACi(AC[14]), .INPRi(1'b0), .DRi(DR[14]), .Instruction(Instruction),
    .Cin(ALU_13_cout), .Cout(ALU_14_cout), .Fi(ALU_Output[14]));
  _1_ALU ALU_11 (
    .Ai_1(AC[12]), .Ai_1_2(AC[10]), .ACi(AC[11]), .INPRi(1'b0), .DRi(DR[11]), .Instruction(Instruction),
    .Cin(ALU_10_cout), .Cout(ALU_11_cout), .Fi(ALU_Output[11]));
  _1_ALU ALU_15 (
    .Ai_1(E), .Ai_1_2(AC[14]), .ACi(AC[15]), .INPRi(1'b0), .DRi(DR[15]), .Instruction(Instruction),
    .Cin(ALU_14_cout), .Cout(ALU_15_cout), .Fi(ALU_Output[15]));

  // Other names for the same wires on the sheet: F0 = ALU_Output[0]; F1 = ALU_Output[1]; F2 = ALU_Output[2];
  //   F3 = ALU_Output[3]; F4 = ALU_Output[4]; F5 = ALU_Output[5]; F6 = ALU_Output[6]; F7 = ALU_Output[7];
  //   F8 = ALU_Output[8]; F9 = ALU_Output[9]; F10 = ALU_Output[10]; F11 = ALU_Output[11]; F12 = ALU_Output[12];
  //   F13 = ALU_Output[13]; F14 = ALU_Output[14]; F15 = ALU_Output[15]
endmodule

module AC (
  input  [15:0] ALU_IN,
  input  r,
  input  p,
  input  [11:0] B,
  input  Clock,
  input  [15:0] T,
  input  [7:0] D,
  output [15:0] Bus_OUT
);

  wire and_1_out, and_2_out, and_3_out, and_4_out, and_5_out, and_6_out, and_7_out, and_8_out, and_9_out,
       or_1_out;

  and and_1 (and_1_out, D[0], T[5]);
  and and_2 (and_2_out, D[1], T[5]);
  and and_3 (and_3_out, D[2], T[5]);
  and and_4 (and_4_out, p, B[11]);
  and and_5 (and_5_out, r, B[9]);
  and and_6 (and_6_out, r, B[7]);
  and and_7 (and_7_out, r, B[6]);
  and and_8 (and_8_out, r, B[5]);
  or or_1 (or_1_out, and_1_out, and_2_out, and_3_out, and_4_out, and_5_out, and_6_out, and_7_out);
  _16_Register_with_adder AC_register (
    .Output(Bus_OUT), .Input(ALU_IN), .Load(or_1_out), .Clock(Clock), .Clear(and_9_out), .INC(and_8_out));
  and and_9 (and_9_out, r, B[11]);
endmodule

module AR (
  input  [15:0] Bus_IN,
  input  I,
  input  [7:0] D,
  input  Clock,
  input  R,
  input  [15:0] T,
  output [15:0] Bus_OUT
);

  wire and_1_out, and_2_out, and_3_out, and_4_out, and_5_out, or_1_out, or_2_out;

  and and_1 (and_1_out, D[5], T[4]);
  and and_2 (and_2_out, R, T[0]);
  and and_3 (and_3_out, ~D[7], I, T[3]);  // AND_Gate
  and and_4 (and_4_out, T[2], ~R);  // AND_Gate
  and and_5 (and_5_out, ~R, T[0]);  // AND_Gate
  or or_1 (or_1_out, and_3_out, and_4_out, and_5_out);
  or or_2 (or_2_out, or_1_out, and_1_out);
  _12_Register_with_adder AR_register (
    .Input(Bus_IN[11:0]), .Load(or_1_out), .INC(or_2_out), .Clock(Clock), .Clear(and_2_out),
    .Output(Bus_OUT[11:0]));

  assign Bus_OUT[15:12] = 4'b0000;
endmodule

module IR (
  input  [15:0] Bus_IN,
  input  Clock,
  input  R,
  input  [15:0] T,
  output [11:0] B,
  output [7:0] D,
  output I,
  output [15:0] Bus_OUT,
  output S
);

  wire and_1_out;

  and and_1 (and_1_out, T[1], ~R);  // AND_Gate
  and and_2 (S, T[3], ~Bus_OUT[15], B[0], D[7]);  // AND_Gate
  Register #(.width(16)) register_1 (.D(Bus_IN), .en(and_1_out), .Q({Bus_OUT[15:12], B}), .clk(Clock));  // open: clr
  Decoder #(.select(3), .enable("false")) decoder_1 (
    .out0(D[0]), .out1(D[1]), .out2(D[2]), .out3(D[3]), .out4(D[4]), .out5(D[5]), .out6(D[6]), .out7(D[7]),
    .sel(Bus_OUT[14:12]));

  assign Bus_OUT[11:0] = B;
  assign I = Bus_OUT[15];
endmodule

module PC (
  input  [15:0] DR,
  input  [15:0] AC,
  input  [11:0] B,
  input  [15:0] Bus_IN,
  input  Clock,
  input  [15:0] T,
  input  r,
  input  p,
  input  R_2,
  input  E,
  input  [7:0] D,
  input  FGI,
  input  FGO,
  output [15:0] Bus_OUT
);

  wire and_1_out, and_2_out, and_3_out, and_4_out, and_5_out, and_6_out, and_7_out, and_8_out, and_9_out,
       and_10_out, and_11_out, or_1_out, or_2_out, or_3_out;

  or or_1 (or_1_out, DR[15], DR[14], DR[13], DR[12], DR[11], DR[10], DR[9], DR[8], DR[7], DR[6], DR[5], DR[4], DR[3], DR[2], DR[1], DR[0]);
  or or_2 (or_2_out, AC[15], AC[14], AC[13], AC[12], AC[11], AC[10], AC[9], AC[8], AC[7], AC[6], AC[5], AC[4], AC[3], AC[2], AC[1], AC[0]);
  and and_1 (and_1_out, ~R_2, T[1]);  // AND_Gate
  and and_2 (and_2_out, R_2, T[2]);
  and and_3 (and_3_out, B[2], r, ~or_2_out);  // AND_Gate
  and and_4 (and_4_out, B[4], r, ~AC[15]);  // AND_Gate
  and and_5 (and_5_out, B[3], r, AC[15]);
  and and_6 (and_6_out, D[6], T[6], ~or_1_out);  // AND_Gate
  and and_7 (and_7_out, r, B[1], ~E);  // AND_Gate
  and and_8 (and_8_out, p, B[9], ~FGI);  // AND_Gate
  and and_9 (and_9_out, p, B[8], FGO);
  or or_3 (or_3_out, and_1_out, and_2_out, and_3_out, and_4_out, and_5_out, and_6_out, and_7_out, and_8_out, and_9_out);
  and and_10 (and_10_out, D[4], T[4]);
  and and_11 (and_11_out, R_2, T[1]);
  _12_Register_with_adder PC_register (
    .Input(Bus_IN[11:0]), .Load(and_10_out), .INC(or_3_out), .Clock(Clock), .Clear(and_11_out),
    .Output(Bus_OUT[11:0]));

  assign Bus_OUT[15:12] = 4'b0000;

  // Other names for the same wires on the sheet: R_t = R_2
endmodule

module TR (
  input  [15:0] Bus_IN,
  input  R,
  input  Clock,
  input  [15:0] T,
  output [15:0] Bus_OUT
);

  wire and_1_out;

  and and_1 (and_1_out, T[0], R);
  Register #(.width(16)) TR (.D(Bus_IN), .en(and_1_out), .Q(Bus_OUT), .clk(Clock));  // open: clr
endmodule

module DR (
  input  [15:0] T,
  input  [15:0] Bus_IN,
  input  Clock,
  input  [7:0] D,
  output [15:0] Bus_OUT
);

  wire and_1_out, and_2_out, or_1_out;

  or or_1 (or_1_out, D[6], D[2], D[1], D[0]);
  and and_1 (and_1_out, T[5], D[6]);
  and and_2 (and_2_out, T[4], or_1_out);
  _16_Register_with_adder u_16_register_with_adder_1 (
    .Output(Bus_OUT), .Input(Bus_IN), .Load(and_2_out), .Clock(Clock), .Clear(1'b0), .INC(and_1_out));
endmodule

module OUTR (
  input  [15:0] Bus_IN,
  input  p,
  input  [11:0] B,
  input  Clock,
  output [3:0] out_5,
  output [3:0] out_6
);

  wire and_1_out;

  and and_1 (and_1_out, p, B[10]);
  Register OUTR (.D(Bus_IN[7:0]), .en(and_1_out), .Q({out_6, out_5}), .clk(Clock));  // open: clr
endmodule

// E flipflop
module E (
  input  r,
  input  Clock,
  input  [11:0] B,
  input  Cout,
  input  [7:0] D,
  input  INP,
  input  [15:0] T,
  output E
);

  wire and_1_out, and_2_out, and_3_out, and_4_out, and_5_out, and_6_out, or_1_out, or_2_out, or_3_out;

  and and_1 (and_1_out, D[1], T[5]);
  or or_1 (or_1_out, B[6], B[7], B[8]);
  and and_2 (and_2_out, r, or_1_out);
  or or_2 (or_2_out, and_2_out, and_1_out);
  and and_3 (and_3_out, Cout, and_1_out);
  and and_4 (and_4_out, r, B[6], INP);
  D_Flip_Flop d_ff_1 (.clk(Clock), .D(or_3_out), .Q(E), .en(or_2_out));  // open: Qn, preset, reset
  or or_3 (or_3_out, and_3_out, and_4_out, and_5_out, and_6_out);
  and and_5 (and_5_out, r, B[7], INP);
  and and_6 (and_6_out, r, B[8], ~E);  // AND_Gate
endmodule

module IEN (
  input  [11:0] B,
  input  p,
  input  Clock,
  input  R,
  input  [15:0] T,
  output IEN
);

  wire and_1_out, and_2_out, and_3_out, or_1_out, or_2_out;

  and and_1 (and_1_out, T[2], R);
  and and_2 (and_2_out, p, B[7]);
  and and_3 (and_3_out, p, B[6]);
  or or_1 (or_1_out, and_3_out, and_1_out);
  or or_2 (or_2_out, and_2_out, or_1_out);
  J_K_Flip_Flop j_k_ff_1 (.J(and_2_out), .clk(Clock), .K(or_1_out), .Q(IEN), .en(or_2_out));  // open: Qn, preset, reset
endmodule

module FGI (
  input  Clock,
  input  [11:0] B,
  input  p,
  output FGI
);

  wire and_1_out, not_1_out;

  and and_1 (and_1_out, B[11], p);
  not not_1 (not_1_out, and_1_out);
  D_Flip_Flop d_ff_1 (.clk(Clock), .D(not_1_out), .Q(FGI), .en(and_1_out));  // open: Qn, preset, reset
endmodule

module FGO (
  input  Clock,
  input  [11:0] B,
  input  p,
  output FGO
);

  wire and_1_out, not_1_out;

  and and_1 (and_1_out, B[10], p);
  not not_1 (not_1_out, and_1_out);
  D_Flip_Flop d_ff_1 (.clk(Clock), .D(not_1_out), .Q(FGO), .en(and_1_out));  // open: Qn, preset, reset
endmodule

module R (
  input  FGI,
  input  FGO,
  input  IEN,
  input  Clock,
  input  [15:0] T,
  output R
);

  wire and_1_out, and_2_out, and_3_out, nor_1_out, or_1_out, or_2_out, or_3_out;

  or or_1 (or_1_out, FGI, FGO);
  and and_1 (and_1_out, or_1_out, IEN, nor_1_out);
  nor nor_1 (nor_1_out, T[0], T[1], T[2]);
  and and_2 (and_2_out, T[2], R);
  or or_2 (or_2_out, and_1_out, and_2_out);
  and and_3 (and_3_out, and_2_out, 1'b0);
  or or_3 (or_3_out, and_1_out, and_3_out);
  D_Flip_Flop d_ff_1 (.clk(Clock), .D(or_3_out), .Q(R), .en(or_2_out));  // open: Qn, preset, reset
endmodule

module SC (
  input  p,
  input  r,
  input  R_2,
  input  INC,
  input  S,
  input  Clock,
  input  Clear,
  input  [7:0] D,
  output [15:0] T
);

  wire and_1_out, and_2_out, and_3_out, and_4_out, and_5_out, and_6_out, and_7_out, and_8_out, and_9_out,
       or_1_out, or_2_out, or_3_out;
  wire [11:0] n12_register_with_adder_1_output;

  and and_1 (and_1_out, R_2, T[2]);
  _12_Register_with_adder u_12_register_with_adder_1 (
    .Input({12{1'b0}}), .Load(or_1_out), .INC(INC), .Clock(and_2_out), .Clear(or_3_out),
    .Output(n12_register_with_adder_1_output));
  or or_1 (or_1_out, p, r, and_1_out, or_2_out);
  and and_2 (and_2_out, ~S, Clock);  // AND_Gate
  or or_2 (or_2_out, and_3_out, and_4_out, and_5_out, and_6_out, and_7_out, and_8_out, and_9_out);
  or or_3 (or_3_out, n12_register_with_adder_1_output[4], Clear);
  and and_3 (and_3_out, T[5], D[0]);
  and and_4 (and_4_out, T[5], D[1]);
  and and_5 (and_5_out, T[5], D[2]);
  and and_6 (and_6_out, T[4], D[3]);
  and and_7 (and_7_out, T[4], D[4]);
  and and_8 (and_8_out, T[5], D[5]);
  and and_9 (and_9_out, T[6], D[6]);
  Decoder #(.select(4), .enable("false")) decoder_1 (
    .out0(T[0]), .out1(T[1]), .out2(T[2]), .out3(T[3]), .out4(T[4]), .out5(T[5]), .out6(T[6]), .out7(T[7]),
    .out8(T[8]), .out9(T[9]), .out10(T[10]), .out11(T[11]), .out12(T[12]), .out13(T[13]), .out14(T[14]),
    .out15(T[15]), .sel(n12_register_with_adder_1_output[3:0]));
endmodule

// Mem_control
module Memory_control (
  input  R,
  input  [7:0] D,
  input  [15:0] T,
  output Load
);

  wire and_1_out, and_2_out, and_3_out, and_4_out;

  and and_1 (and_1_out, R, T[1]);
  and and_2 (and_2_out, D[3], T[4]);
  and and_3 (and_3_out, D[5], T[4]);
  and and_4 (and_4_out, D[6], T[6]);
  or or_1 (Load, and_1_out, and_2_out, and_3_out, and_4_out);
endmodule

module BUS_control (
  input  [15:0] T,
  input  [7:0] D,
  input  I,
  input  R,
  input  p,
  input  [11:0] B,
  output [2:0] BUS_Output
);

  wire AC_out, and_1_out, and_2_out, and_3_out, and_4_out, and_5_out, and_6_out, and_7_out, and_8_out,
       and_9_out, and_10_out, AR_out, DR_out, IR_out, MR_out, or_1_out, PC_out, TR_out;

  and and_1 (and_1_out, D[5], T[5]);
  and and_2 (and_2_out, D[2], T[5]);
  and and_3 (and_3_out, p, B[10]);
  and and_4 (and_4_out, ~R, T[1]);  // AND_Gate
  or or_1 (or_1_out, D[0], D[1], D[2], D[6]);
  and and_5 (and_5_out, D[4], T[4]);
  and and_6 (and_6_out, D[5], T[4]);
  and and_7 (and_7_out, D[6], T[6]);
  and and_8 (and_8_out, D[3], T[4]);
  and and_9 (and_9_out, ~D[7], I, T[3]);  // AND_Gate
  and and_10 (and_10_out, T[4], or_1_out);
  or AR (AR_out, and_5_out, and_1_out);
  or PC (PC_out, T[0], and_6_out);
  or DR (DR_out, and_7_out, and_2_out);
  or AC (AC_out, and_8_out, and_3_out);
  and IR (IR_out, ~R, T[2]);  // AND_Gate
  and TR (TR_out, R, T[1]);
  or MR (MR_out, and_9_out, and_4_out, and_10_out);
  Priority_Encoder priority_encoder_1 (
    .in0(1'b0), .in1(AR_out), .in2(PC_out), .in3(DR_out), .in4(AC_out), .in5(IR_out), .in6(TR_out),
    .in7(MR_out), .out(BUS_Output));  // open: en_in, gs, en_out
endmodule
